# Fritzing sketch rfid-rc522 (saved by Fritzing 0.9.3b)
circuit board: 8.46667cm x 5.64444cm
breadboards: 1

parts:
  Componente1 = RFID-RC522-v2
  R2 = Resistor [tolerance=±5% resistance=220 package=THT]
  Part1 = Arduino Uno (Rev3) - ICSP
  LED1 = smd LED [color="Red (633nm)" package="0805 [SMD]"]

nets:
  N1: Componente1.SDA, Part1.D2
  N2: Componente1.SCK, Part1.D5_PWM
  N3: Componente1.MOSI, Part1.D7
  N4: Componente1.MISO, Part1.D6_PWM
  GND: Componente1.GND, Part1.GND, LED1.anode
  N5: Componente1.RST, Part1.D1/TX
  3.3V: Componente1.3.3V, Part1.3V3
  N6: R2.Pin_0, Part1.D4
  N7: R2.Pin_1, LED1.cathode

custom parts:
  RFID-RC522-v2: A simple China made RFID-RC522 Reader; do check the pin labels, as this is a MFRC522 based clone.

// code stored in the sketch: Untitled2.ino
#define SS_PIN 4  //D2
#define RST_PIN 5 //D1
#define LED_R 2 //define red LED
#include <SPI.h>
#include <MFRC522.h>

MFRC522 mfrc522(SS_PIN, RST_PIN);   // Create MFRC522 instance/object.
int variable = 0;
void setup() 
{
  Serial.begin(9600);   // Initiate a serial communication
  SPI.begin();      // Initiate  SPI bus
  mfrc522.PCD_Init();   // Initiate MFRC522
  pinMode(LED_R, OUTPUT);
  Serial.println("Show your card:");
}
void loop() 
{
  // Look for new cards
  if ( ! mfrc522.PICC_IsNewCardPresent()) 
  {
    return;
  }
  // Select one of the cards
  if ( ! mfrc522.PICC_ReadCardSerial()) 
  {
    return;
  }
  //Show UID on serial monitor
  Serial.print(" UID tag :");
  String content= "";
  byte letter;
  for (byte i = 0; i < mfrc522.uid.size; i++) 
  {
     Serial.print(mfrc522.uid.uidByte[i] < 0x10 ? " 0" : " ");
     Serial.print(mfrc522.uid.uidByte[i], HEX);
     content.concat(String(mfrc522.uid.uidByte[i] < 0x10 ? " 0" : " "));
     content.concat(String(mfrc522.uid.uidByte[i], HEX));
  }
  content.toUpperCase();
  Serial.println();
  if (content.substring(1) == "C1 9A 15 44") //change UID of the card that you want to give access
  {
    Serial.println(" Authorized Access ");
    Serial.println(" Welcome Mandalan ");
    delay(500);
    digitalWrite(LED_R, HIGH);
    delay(5000);
    digitalWrite(LED_R, LOW);
  }
  
  else   {
    Serial.println(" Access Denied ");
    delay(3000);
  }
}
